# Fritzing sketch batedor de panela (esquemático) (saved by Fritzing 0.9.3b)
breadboards: 1

parts:
  Part1 = Arduino Nano (Rev3.0) (ICSP)
  J1 = Basic Servo
  BAT1 = BC9VPC [package=bc9vpc]
  U1 = POT [package=alps_pot]

nets:
  GND: Part1.GND, J1.gnd, BAT1.V-, U1.A
  N1: Part1.D9, J1.pulse
  N2: Part1.VIN, BAT1.V+
  5V: Part1.5V, J1.vcc, U1.E
  N3: Part1.A0, U1.S
